// Logisim project Morse_Code.circ as structural Verilog: 2 circuits, main circuit main
module main (
  input  _1,
  input  _2,
  input  _3,
  input  _4,
  input  _5,
  input  _6,
  input  _7,
  input  _8,
  input  _9,
  input  nLoad___Shift
);

  wire and_1_out, and_2_out, and_3_out, and_4_out, and_5_out, and_6_out, and_7_out, and_8_out, and_9_out,
       and_10_out, and_11_out, and_12_out, and_13_out, and_14_out, and_15_out, and_16_out, and_17_out,
       and_18_out, and_19_out, and_20_out, and_21_out, and_22_out, and_23_out, and_24_out, and_25_out,
       and_26_out, and_27_out, and_28_out, and_29_out, and_30_out, and_31_out, and_32_out, and_33_out,
       and_34_out, and_35_out, and_36_out, and_37_out, and_38_out, and_39_out, and_40_out, and_41_out,
       and_42_out, buffer_1_out, j_k_ff_1_q, j_k_ff_2_q, j_k_ff_3_q, j_k_ff_4_q, j_k_ff_5_q, Main_Clock_out,
       n7_segment_1_a, n7_segment_1_b, n7_segment_1_c, n7_segment_1_d, n7_segment_1_e, n7_segment_1_f,
       n7_segment_1_g, not_1_out, not_2_out, not_3_out, not_4_out, not_5_out, not_6_out, not_7_out,
       not_8_out, not_9_out, not_10_out, not_11_out, not_12_out, not_13_out, not_14_out, or_1_out, or_2_out,
       or_3_out, or_4_out, or_5_out, or_6_out, or_7_out, or_8_out, or_9_out, or_10_out, or_11_out, or_12_out,
       or_13_out, or_14_out, or_15_out, or_16_out, or_17_out, register_1_q, register_2_q, register_3_q,
       register_4_q, register_5_q, t_ff_1_q, t_ff_1_qn, xor_1_out;

  not not_1 (not_1_out, or_9_out);
  not not_2 (not_2_out, or_8_out);
  not not_3 (not_3_out, or_7_out);
  not not_4 (not_4_out, or_6_out);
  and and_1 (and_1_out, not_1_out, or_8_out, not_3_out);
  and and_2 (and_2_out, not_1_out, not_3_out, or_6_out);
  and and_3 (and_3_out, not_1_out, not_2_out, or_7_out);
  and and_4 (and_4_out, not_1_out, or_8_out, not_3_out);
  and and_5 (and_5_out, not_1_out, not_2_out, or_7_out);
  and and_6 (and_6_out, not_1_out, or_7_out, not_4_out);
  and and_7 (and_7_out, not_1_out, or_8_out);
  and and_8 (and_8_out, not_1_out, or_7_out, or_6_out);
  and and_9 (and_9_out, not_1_out, or_8_out);
  and and_10 (and_10_out, or_9_out, not_2_out, not_3_out, not_4_out);
  and and_11 (and_11_out, not_1_out, or_8_out, or_6_out);
  and and_12 (and_12_out, not_1_out, or_8_out, or_7_out);
  and and_13 (and_13_out, or_9_out, not_2_out, not_3_out);
  or or_1 (or_1_out, and_1_out, and_2_out, and_3_out);
  or or_2 (or_2_out, and_4_out, and_5_out, and_6_out);
  or or_3 (or_3_out, and_7_out, and_8_out);
  or or_4 (or_4_out, and_9_out, and_10_out);
  or or_5 (or_5_out, and_11_out, and_12_out, and_13_out);
  Clock Main_Clock (.out(Main_Clock_out));
  or or_6 (or_6_out, _1, _3, _5, _7, _9);
  or or_7 (or_7_out, _2, _3, _6, _7);
  or or_8 (or_8_out, _4, _5, _6, _7);
  or or_9 (or_9_out, _8, _9);
  and and_14 (and_14_out, Main_Clock_out, not_5_out);
  not not_5 (not_5_out, nLoad___Shift);
  and and_15 (and_15_out, nLoad___Shift, Main_Clock_out);
  and and_16 (and_16_out, nLoad___Shift, j_k_ff_1_q, j_k_ff_2_q);
  or or_10 (or_10_out, and_16_out, and_14_out);
  not not_6 (not_6_out, nLoad___Shift);
  not not_7 (not_7_out, nLoad___Shift);
  J_K_Flip_Flop j_k_ff_1 (
    .J(1'b1), .clk(and_15_out), .K(1'b1), .Q(j_k_ff_1_q), .reset(not_6_out));  // open: Qn, preset, en
  and and_17 (and_17_out, or_8_out, or_9_out);
  Register #(.width(1)) register_1 (.D(or_5_out), .en(1'b1), .Q(register_1_q), .clk(or_10_out));  // open: clr
  and and_18 (and_18_out, or_7_out, or_9_out);
  or or_11 (or_11_out, and_18_out, and_17_out);
  and and_19 (and_19_out, not_7_out, or_1_out);
  and and_20 (and_20_out, not_7_out, or_2_out);
  and and_21 (and_21_out, not_7_out, or_3_out);
  and and_22 (and_22_out, not_7_out, or_4_out);
  and and_23 (and_23_out, nLoad___Shift, register_1_q);
  J_K_Flip_Flop j_k_ff_2 (
    .J(j_k_ff_1_q), .clk(and_15_out), .K(j_k_ff_1_q), .Q(j_k_ff_2_q), .reset(not_6_out));  // open: Qn, preset, en
  and and_24 (and_24_out, j_k_ff_2_q, j_k_ff_1_q);
  and and_25 (and_25_out, or_6_out, not_8_out);
  and and_26 (and_26_out, not_8_out, or_7_out);
  and and_27 (and_27_out, or_8_out, not_8_out);
  not not_8 (not_8_out, or_11_out);
  or or_12 (or_12_out, and_22_out, and_23_out);
  Register #(.width(1)) register_2 (.D(or_12_out), .en(1'b1), .Q(register_2_q), .clk(or_10_out));  // open: clr
  _7_Segment u_7_segment_1 (
    .B3(and_28_out), .B2(and_27_out), .B1(and_26_out), .B0(and_25_out), .A(n7_segment_1_a),
    .B(n7_segment_1_b), .C(n7_segment_1_c), .D(n7_segment_1_d), .E(n7_segment_1_e), .F(n7_segment_1_f),
    .G(n7_segment_1_g));
  and and_28 (and_28_out, or_9_out, not_9_out);
  not not_9 (not_9_out, or_11_out);
  and and_29 (and_29_out, nLoad___Shift, register_2_q);
  not not_10 (not_10_out, nLoad___Shift);
  and and_30 (and_30_out, and_24_out, nLoad___Shift);
  or or_13 (or_13_out, and_21_out, and_29_out);
  not not_11 (not_11_out, j_k_ff_1_q);
  _7_Segment_Display u_7_segment_display_1 (
    .g(n7_segment_1_g), .f(n7_segment_1_f), .a(n7_segment_1_a), .b(n7_segment_1_b), .e(n7_segment_1_e),
    .d(n7_segment_1_d), .c(n7_segment_1_c));  // open: dp
  LED Invalid_BCD (.in(or_11_out));
  Register #(.width(1)) register_3 (.D(or_13_out), .en(1'b1), .Q(register_3_q), .clk(or_10_out));  // open: clr
  LED Morse_Code (.in(and_42_out));
  and and_31 (and_31_out, nLoad___Shift, register_3_q);
  or or_14 (or_14_out, and_20_out, and_31_out);
  J_K_Flip_Flop j_k_ff_3 (
    .J(1'b1), .clk(and_30_out), .K(1'b1), .Q(j_k_ff_3_q), .en(1'b1), .reset(not_10_out));  // open: Qn, preset
  Register #(.width(1)) register_4 (.D(or_14_out), .en(1'b1), .Q(register_4_q), .clk(or_10_out));  // open: clr
  and and_32 (and_32_out, not_11_out, j_k_ff_2_q);
  xor xor_1 (xor_1_out, j_k_ff_1_q, j_k_ff_2_q);
  J_K_Flip_Flop j_k_ff_4 (
    .J(j_k_ff_3_q), .clk(and_30_out), .K(j_k_ff_3_q), .Q(j_k_ff_4_q), .en(1'b1), .reset(not_10_out));  // open: Qn, preset
  and and_33 (and_33_out, nLoad___Shift, register_4_q);
  and and_34 (and_34_out, j_k_ff_3_q, j_k_ff_4_q);
  and and_35 (and_35_out, not_9_out, nLoad___Shift);
  or or_15 (or_15_out, and_19_out, and_33_out);
  J_K_Flip_Flop j_k_ff_5 (
    .J(and_34_out), .clk(and_30_out), .K(and_34_out), .Q(j_k_ff_5_q), .en(1'b1), .reset(not_10_out));  // open: Qn, preset
  Register #(.width(1)) register_5 (.D(or_15_out), .en(1'b1), .Q(register_5_q), .clk(or_10_out));  // open: clr
  not not_12 (not_12_out, nLoad___Shift);
  and and_36 (and_36_out, j_k_ff_5_q, j_k_ff_3_q);
  and and_37 (and_37_out, j_k_ff_5_q, j_k_ff_4_q);
  not not_13 (not_13_out, register_5_q);
  or or_16 (or_16_out, and_36_out, and_37_out);
  and and_38 (and_38_out, register_5_q, and_32_out);
  and and_39 (and_39_out, not_13_out, xor_1_out);
  not not_14 (not_14_out, t_ff_1_q);
  and and_40 (and_40_out, not_14_out, or_16_out);
  buf buffer_1 (buffer_1_out, or_16_out);
  or or_17 (or_17_out, and_38_out, and_39_out);
  T_Flip_Flop t_ff_1 (
    .clk(buffer_1_out), .T(and_40_out), .Q(t_ff_1_q), .Qn(t_ff_1_qn), .reset(not_12_out), .en(1'b1));  // open: preset
  and and_41 (and_41_out, or_17_out, t_ff_1_qn);
  and and_42 (and_42_out, and_35_out, and_41_out);

  // Notes on the sheet:
  //   Enable
  //   C1 - Clock
  //   C0
  //                                  SEND MORSE CODE SIGNAL
endmodule

module _7_Segment (
  input  B3,
  input  B2,
  input  B1,
  input  B0,
  output A,
  output B,
  output C,
  output D,
  output E,
  output F,
  output G
);

  wire and_1_out, and_2_out, and_3_out, and_4_out, and_5_out, and_6_out, and_7_out, and_8_out, and_9_out,
       and_10_out, and_11_out, and_12_out, and_13_out, and_14_out, and_15_out, and_16_out, not_1_out,
       not_2_out, not_3_out, not_4_out, not_5_out, not_6_out, not_7_out, not_8_out, not_9_out, not_10_out,
       not_11_out, not_12_out, not_13_out, not_14_out, not_15_out, not_16_out, not_17_out, not_18_out,
       not_19_out, not_20_out, not_21_out;

  not not_1 (not_1_out, B2);
  and and_1 (and_1_out, not_1_out, not_2_out);
  not not_2 (not_2_out, B0);
  and and_2 (and_2_out, B2, B0);
  not not_3 (not_3_out, B2);
  not not_4 (not_4_out, B1);
  and and_3 (and_3_out, not_4_out, not_5_out);
  not not_5 (not_5_out, B0);
  and and_4 (and_4_out, B1, B0);
  not not_6 (not_6_out, B1);
  or or_1 (C, not_6_out, B0, B2);
  not not_7 (not_7_out, B2);
  and and_5 (and_5_out, not_7_out, not_8_out);
  not not_8 (not_8_out, B0);
  not not_9 (not_9_out, B2);
  and and_6 (and_6_out, not_9_out, B1);
  and and_7 (and_7_out, B1, not_10_out);
  not not_10 (not_10_out, B0);
  not not_11 (not_11_out, B1);
  and and_8 (and_8_out, B2, not_11_out, B0);
  not not_12 (not_12_out, B2);
  and and_9 (and_9_out, not_12_out, not_13_out);
  not not_13 (not_13_out, B0);
  and and_10 (and_10_out, B1, not_14_out);
  not not_14 (not_14_out, B0);
  not not_15 (not_15_out, B1);
  and and_11 (and_11_out, not_15_out, not_16_out);
  not not_16 (not_16_out, B0);
  and and_12 (and_12_out, B2, not_17_out);
  not not_17 (not_17_out, B1);
  and and_13 (and_13_out, B2, not_18_out);
  not not_18 (not_18_out, B0);
  not not_19 (not_19_out, B2);
  and and_14 (and_14_out, not_19_out, B1);
  and and_15 (and_15_out, B2, not_20_out);
  not not_20 (not_20_out, B1);
  and and_16 (and_16_out, B2, not_21_out);
  not not_21 (not_21_out, B0);
  or or_2 (A, and_1_out, B1, and_2_out, B3);
  or or_3 (B, not_3_out, and_3_out, and_4_out);
  or or_4 (D, and_5_out, and_6_out, and_7_out, and_8_out, B3);
  or or_5 (E, and_9_out, and_10_out);
  or or_6 (F, and_11_out, and_12_out, and_13_out, B3);
  or or_7 (G, and_14_out, and_15_out, and_16_out, B3);
endmodule
